# Fritzing sketch Lab 2 (saved by Fritzing 0.9.3b)
breadboards: 1

parts:
  Part1 = Arduino Uno (Rev3)
  S1 = Pushbutton [package="[THT]"]
  S2 = Pushbutton [package="[THT]"]
  R1 = Resistor [tolerance=±5% resistance=10k package=THT]
  R2 = Resistor [tolerance=±5% resistance=10k package=THT]
  Potential_Meter = Rotary Potentiometer (Small) [maximum_resistance=100kΩ package=THT]
  LED1 = LED - 5mm [color="Red (633nm)" package="5 mm [THT]"]
  LED2 = LED - 5mm [color="Red (633nm)" package="5 mm [THT]"]
  R4 = Resistor [tolerance=±5% resistance=330 package=THT]
  R5 = Resistor [tolerance=±5% resistance=330 package=THT]
  Touch_Sensor = Rotary Potentiometer (Small) [maximum_resistance=100kΩ package=THT]

nets:
  N1: Part1.A0, Potential_Meter.wiper
  N2: Part1.A1, Touch_Sensor.wiper
  N3: Part1.GND, S1.Pin_2, S2.Pin_2, Potential_Meter.leg1, R4.Pin_1, R5.Pin_1, Touch_Sensor.leg1
  N4: Part1.D2, S1.Pin_3, S1.Pin_4, R1.Pin_0
  N5: Part1.D3_PWM, S2.Pin_3, S2.Pin_4, R2.Pin_0
  N6: Part1.D6_PWM, LED1.anode
  N7: Part1.D7, LED2.anode
  N8: Part1.5V, R1.Pin_1, R2.Pin_1, Potential_Meter.leg2, Touch_Sensor.leg2
  N9: LED1.cathode, R4.Pin_0
  N10: LED2.cathode, R5.Pin_0
